// Digital circuit computer_foxbay.dig as structural Verilog
module computer_foxbay (
  input  programClock,
  input  [15:0] At_2,
  output [15:0] At
);

  wire and_1_out, and_2_out, and_3_out, and_5_out, and_6_out, and_7_out, \break , clock, d_ff_1_q,
       enable_dev, enable_dev_btn, enable_dev_fbswitch, enable_dev_midi, enable_gram, enable_ram, not_1_out,
       or_1_out, or_3_out, register_1_q, reset_break_out, rs_ff_as_1_q, startClock_out, step_out,
       stopClock_out, sub_1_s, write_bus;
  wire [1:0] enable_d;
  wire [7:0] S_out;
  wire [15:0] addr, addr_dec, addr_dec_internal, device_offset_d, in_proc, instruction, mask_d, out_dev,
       out_gram, out_proc, out_ram, ptr_inst, ramdualport_1_d;

  Button step (.out(step_out));
  Button startClock (.out(startClock_out));
  or or_1 (or_1_out, stopClock_out, d_ff_1_q);
  Button stopClock (.out(stopClock_out));
  LED u_break (.in(d_ff_1_q));
  Button reset_break (.out(reset_break_out));
  Button LEFT (.out(S_out[5]));
  RS_FF_AS rs_ff_as_1 (.S(startClock_out), .R(or_1_out), .Q(rs_ff_as_1_q));  // open: nQ
  Button UP (.out(S_out[7]));
  Button DOWN (.out(S_out[6]));
  and and_1 (and_1_out, programClock, rs_ff_as_1_q);
  D_FF d_ff_1 (.D(and_2_out), .C(or_3_out), .Q(d_ff_1_q));  // open: nQ
  Button RIGHT (.out(S_out[4]));
  or or_2 (clock, step_out, and_1_out);
  Button Z (.out(S_out[2]));
  or or_3 (or_3_out, reset_break_out, clock);
  and and_2 (and_2_out, \break , ~reset_break_out);  // And
  Button A (.out(S_out[3]));
  Button S (.out(S_out[1]));
  Button X (.out(S_out[0]));
  assign out_dev = enable_dev_btn ? {{8{1'b0}}, S_out} : 16'bz;  // Driver driver_1
  RAMDualAccess #(.AddrBits(16), .Bits(16)) ramdualaccess_1 (
    .str(write_bus), .C(clock), .ld(1'b1), .A1(addr), .Din1(out_proc), .A2(At_2), .D2(At));  // open: D1
  Seven_Seg_Hex seven_seg_hex_1 (.d(At[15:12]), .dp(1'b0));
  Seven_Seg_Hex seven_seg_hex_2 (.d(At[11:8]), .dp(1'b0));
  // Probe PC on ptr_inst
  ROM #(.bigEndian("true"), .AddrBits(16), .isProgramMemory("true"), .Bits(16)) \program  (
    .A(ptr_inst), .sel(1'b1), .D(instruction));
  ROM #(.AddrBits(3), .Bits(16)) device_offset (.A(addr_dec_internal[2:0]), .sel(1'b1), .D(device_offset_d));
  Demultiplexer demultiplexer_1 (.sel(addr_dec[0]), .in(out_proc[0]));  // open: out_0, out_1
  ROM #(.Bits(2)) enable (.A(addr[14:13]), .sel(1'b1), .D(enable_d));
  ROM #(.Bits(16)) mask (.A(addr[14:13]), .D(mask_d));  // open: sel
  and and_3 (and_3_out, enable_dev_midi, write_bus);
  Seven_Seg_Hex seven_seg_hex_3 (.d(At[7:4]), .dp(1'b0));
  // Probe I on instruction
  Decoder #(.Selector_Bits(2)) decoder_1 (
    .sel(enable_d), .out_0(enable_ram), .out_1(enable_gram), .out_2(enable_dev));  // open: out_3
  assign addr_dec_internal = mask_d & addr;  // And and_4, 16 bits wide
  Sub sub_1 (.a(addr_dec_internal[0]), .b(device_offset_d[0]), .s(sub_1_s));  // open: c_i, c_o
  Seven_Seg_Hex seven_seg_hex_4 (.d(At[3:0]), .dp(1'b0));
  // bus_driver bus_driver_1: pin names not known; wires that end beside it: sub_1_s, enable_dev, out_dev, addr_dec, in_proc
  cpu_proc16b1 cpu_proc16b1_1 (
    .inst(instruction), .bus_in(in_proc), .clock(clock), .ptr_inst(ptr_inst), .bus_addr(addr),
    .bus_out(out_proc), .bus_write(write_bus), .\break (\break ));
  // Probe addr on addr
  // Probe on addr
  // Probe on addr
  // Probe out_proc on out_proc
  // Probe on out_proc
  // Probe on out_proc
  bus_driver bus_driver_2 (
    .oaddr(addr_dec), .oout(in_proc), .iaddr(addr_dec_internal), .ie(enable_ram), .iout(out_ram));  // open: oe
  bus_driver bus_driver_3 (
    .oaddr(addr_dec), .oout(in_proc), .iaddr(addr_dec_internal), .ie(enable_gram), .iout(out_gram));  // open: oe
  // MIDI #(.midiInstrument("Violin")) midi_1: pin names not known; wires that end beside it: clock
  // Probe on write_bus
  and and_5 (and_5_out, enable_ram, write_bus);
  and and_6 (and_6_out, enable_dev_fbswitch, write_bus);
  and and_7 (and_7_out, enable_gram, write_bus);
  not not_1 (not_1_out, write_bus);
  Register register_1 (.D(out_proc[0]), .C(clock), .en(and_6_out), .Q(register_1_q));
  RAMDualPort #(.AddrBits(14), .Bits(16)) ramdualport_1 (
    .A(addr_dec[13:0]), .Din(out_proc), .str(and_5_out), .C(clock), .ld(1'b1), .D(ramdualport_1_d));
  GraphicCard #(.graphicHeight(64), .graphicWidth(64), .Bits(16)) graphiccard_1 (
    .A(addr_dec[12:0]), .str(and_7_out), .C(clock), .ld(not_1_out), .B(register_1_q), .D(out_gram));
  assign out_ram = enable_ram ? ramdualport_1_d : 16'bz;  // Driver driver_2
  assign out_gram = and_7_out ? out_proc : 16'bz;  // Driver driver_3
  // Pins of 1 and 16 bits meet at out_proc
  // Pins of 1 and 16 bits meet at addr_dec
  // Pins of 1 and 16 bits meet at addr_dec_internal
  // Pins of 1 and 16 bits meet at device_offset_d

  // Notes on the sheet:
  //   programClock: Hz: 1000
  //   clock
  //   button device
  //   bits 15-8 are 0
  //   7 6543210
  //   UDLRABXY
  //   TODO: program tests
  //   Address map:
  //   0x0000 - 0x3FFF (16Ki) RAM
  //   0x4000 - 0x5FFF (8Ki) video memory
  //   0x6000 - 0x7FFF (8Ki) devices
  //   0x8000 - 0xFFFF (32Ki) unusable
  //   TODO better address space layout
  //   devices:
  //   0x6000: button inputs
  //   0x6001: framebuffer switch
  //   0x6002: midi flags register
  //   0x6003: midi volume register
  //   0x6004: midi note register
  //   address bus test instrumentation
  //   program memory
  //   bus controller
  //   midi device
  //   0x00: midi flags
  //   .......0: enable
  //   .......1: OnOff
  //   0x01: midi note
  //   0x02: midi volume
  //   contents of program (hex, n*v repeats v):
  //   6000,8d02,0,9104,0,a00f
  //   contents of device_offset (hex, n*v repeats v):
  //   0,1,2,2,2
  //   contents of enable (hex, n*v repeats v):
  //   0,1,0,2
  //   contents of mask (hex, n*v repeats v):
  //   7fff,1fff,7fff,1fff
  //   cpu
  //   RAM
  //   graphic RAM + fbswitch device
  //   fbswitch device:
  //   bit 0 is a 1-bit register that
  //   controls the active framebuffer
  //   all other bits are unconnected
endmodule
